# Fritzing sketch Arduino APRS tracker v2 (saved by Fritzing 0.9.3b)
circuit board: 8.45259cm x 7.85467cm
breadboards: 1

parts:
  TNC = Arduino Pro Mini (5V)
  R1 = TRIMPOT [package=trim_pot_pth]
  C1 = Capacitor [package=axial-5mm]
  TRRS1 = Audio Jack (TRRS) 3.5mm [part_number="LUMBERG JEITA RC-5325A" package="RC-5325A [SMD]"]
  C2 = Capacitor [package=axial-5mm]
  R4 = Resistor [tolerance=±5% resistance=1k package=THT]
  R2 = Resistor [tolerance=±5% resistance=10k package=THT]
  R3 = Resistor [tolerance=±5% resistance=10k package=THT]
  J1 = female pin header, 2 pins [form="♀ (female)"]
  Proc = Arduino Pro Mini (5V)
  GPS = mystery part, 4 pins [chip_label=GPS]
  Q1 = NPN-Transistor [package="TO92 [THT]"]

nets:
  N1: TNC.TXO, Proc.RXI
  N2: TNC.RXI, Proc.TXO
  N3: TNC.VCC, R3.Pin_1
  GND: TNC.GND, R1.CW, TRRS1.SLEEVE, R2.Pin_1, J1.pin2, Proc.GND, GPS.pin4, Q1.C
  N4: TNC.RAW, J1.pin1, Proc.RAW
  N5: TNC.D10, R4.Pin_1
  N6: TNC.D6, R1.CCW
  N7: R1.WIPER, C1.2
  N8: C1.1, TRRS1.RING2
  N9: TRRS1.TIP, C2.2
  N10: TRRS1.RING1, Q1.E
  N11: C2.1, R2.Pin_0, R3.Pin_0
  N12: R4.Pin_0, Q1.B
  N13: Proc.VCC, GPS.pin1
  N14: Proc.MOSI, GPS.pin2
  N15: Proc.D10, GPS.pin3
