# Fritzing sketch Arduino APRS tracker (saved by Fritzing 0.9.3b)
circuit board: 5.89081cm x 6.62408cm
breadboards: 1

parts:
  J1 = male pin header, 2 pins [form="♂ (male)"]
  J2 = male pin header, 4 pins [form="♂ (male)"]
  Part1 = Arduino Pro Mini (5V)
  Q1 = NPN-Transistor [package="TO92 [THT]"]
  J4 = Generic male header - 4 pins [form="♂ (male)" package=THT]
  R1 = Resistor [tolerance=±5% resistance=1k package=THT]
  C1 = Ceramic Capacitor [capacitance=100nF package="100 mil [THT, multilayer]"]
  R2 = Trimmer Potentiometer [maximum_resistance=10kΩ package=THT]
  R3 = Resistor [tolerance=±5% resistance=10 package=THT]
  R4 = Resistor [tolerance=±5% resistance=10 package=THT]
  C2 = Ceramic Capacitor [capacitance=10nF package="100 mil [THT, multilayer]"]
  Part2 = Arduino Pro Mini (5V)

nets:
  N1: J1.pin1, Part1.RAW
  GND: J1.pin2, J2.pin4, Part1.GND, Q1.C, J4.gnd_blue, R2.leg1, R4.Pin_0, Part2.GND
  N2: J2.pin1, Part2.VCC
  N3: J2.pin2, Part2.D10
  N4: Part1.A0, R3.Pin_1, R4.Pin_1, C2.0
  N5: Part1.D10, R1.Pin_0
  N6: Part1.D6, R2.wiper
  N7: Part1.RXI, Part2.D3
  N8: Q1.E, J4.ptt_bare
  N9: Q1.B, R1.Pin_1
  N10: J4.tx_red, C1.1
  N11: J4.rx_green, C2.1
  N12: C1.0, R2.leg2

custom parts:
  Generic male header - 4 pins: Generic male header
