# Fritzing sketch Arduino APRS tracker v5 (saved by Fritzing 0.9.3b)
breadboards: 1

parts:
  TNC1 = Arduino Pro Mini (5V)
  Proc1 = Arduino Pro Mini (5V)
  GPS1 = mystery part, 4 pins [chip_label=?]
  Cout1 = Electrolytic Capacitor [capacitance=0.47mF package="200 mil [THT, electrolytic]"]
  Cin1 = Electrolytic Capacitor [capacitance=0.22mF package="200 mil [THT, electrolytic]"]
  L7808CV1 = Voltage Regulator [package=to-220-alt]
  R1 = Resistor [tolerance=±5% resistance=1k package=THT]
  R2 = Resistor [tolerance=±5% resistance=10k package=THT]
  C1_-_10nF = Capacitor [package=cap-pth-small2]
  BC548 = NPN-Transistor [package="TO92 [THT]"]
  R3 = TRIMPOT [package=trim_pot_pth]
  R4 = Resistor [tolerance=±5% resistance=10k package=THT]
  C2_100nF = Capacitor [package=cap-pth-small2]
  J1_-_pwr_in = Screw terminal - 2 pins [package=THT]
  p1=gnd_p2=tx_p3=ptt_p4=rx = screw terminal, 4 pins
  DS1 = DS18B20 1-Wire Temperature Sensor [part_number=DS18B20]
  R5 = Resistor [tolerance=±5% resistance=4.7k package=THT]
  J3_-_bcn_btn = Screw terminal - 2 pins [package=THT]
  R6 = Resistor [tolerance=±5% resistance=10k package=THT]
  R7 = Resistor [tolerance=±5% resistance=220 package=THT]
  R8 = Resistor [tolerance=±5% resistance=220 package=THT]
  R9 = Resistor [tolerance=±5% resistance=10k package=THT]
  R10 = Resistor [tolerance=±5% resistance=10k package=THT]
  LED_TX = LED - 3mm [color="Red (633nm)" package="3 mm [THT]"]
  LED_FIX = LED - 3mm [color="Red (633nm)" package="3 mm [THT]"]
  BC547 = NPN-Transistor [package="TO92 [THT]"]
  R11 = Resistor [tolerance=±5% resistance=1k package=THT]
  D1 = Rectifier Diode [part_number=1N4007 package="300 mil [THT]"]
  U1 = RELAY [package=relay-g5q]
  fan_sw = Screw terminal - 2 pins [package=THT]

nets:
  N1: TNC1.RAW, Proc1.RAW, Cout1.+, L7808CV1.OUT
  VCC: TNC1.VCC, R2.Pin_0, DS1.VDD, R5.Pin_0
  N2: TNC1.A0, R2.Pin_1, C1_-_10nF.1, R4.Pin_1
  N3: TNC1.D10, R1.Pin_1
  N4: TNC1.D6, R3.CCW
  GND: TNC1.GND, Proc1.GND, GPS1.pin4, Cout1.-, Cin1.-, L7808CV1.GND, BC548.C, R3.CW, R4.Pin_0, J1_-_pwr_in.pin2, p1=gnd_p2=tx_p3=ptt_p4=rx.pin1, DS1.GND, R6.Pin_0, R8.Pin_1, R9.Pin_1, R10.Pin_1, BC547.E
  N5: TNC1.RXI, Proc1.D2
  N6: TNC1.TXO, Proc1.D3
  N7: Proc1.VCC, GPS1.pin1, J3_-_bcn_btn.pin2, D1.cathode, U1.COIL2
  N8: Proc1.A1, R7.Pin_1, R8.Pin_0
  N9: Proc1.SCK, LED_FIX.anode
  N10: Proc1.MISO, GPS1.pin3
  N11: Proc1.MOSI, GPS1.pin2
  N12: Proc1.D9, LED_TX.anode
  N13: Proc1.D8, J3_-_bcn_btn.pin1, R6.Pin_1
  N14: Proc1.D7, DS1.DQ, R5.Pin_1
  N15: Proc1.D4, R11.Pin_0
  N16: Cin1.+, L7808CV1.IN, J1_-_pwr_in.pin1, R7.Pin_0
  N17: R1.Pin_0, BC548.B
  N18: C1_-_10nF.2, p1=gnd_p2=tx_p3=ptt_p4=rx.pin4
  N19: BC548.E, p1=gnd_p2=tx_p3=ptt_p4=rx.pin3
  N20: R3.WIPER, C2_100nF.2
  N21: C2_100nF.1, p1=gnd_p2=tx_p3=ptt_p4=rx.pin2
  N22: R9.Pin_0, LED_FIX.cathode
  N23: R10.Pin_0, LED_TX.cathode
  N24: BC547.B, R11.Pin_1
  N25: BC547.C, D1.anode, U1.COIL1
  N26: U1.MAIN, fan_sw.pin1
  N27: U1.NO, fan_sw.pin2

custom parts:
  Arduino Pro Mini (5V): It's blue! It's thin! It's the Arduino Pro Mini! SparkFun's minimal design approach to Arduino. This is a 5V Arduino running the 16MHz bootloader. Arduino Pro Mini does not come with connectors populated so that you can solder in any connector or wire with any orientation you need. We recommend first time Arduino users start with the Uno R3. It's a great board that will get you up and running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
